# Fritzing sketch R01_3 sensores_N1 (saved by Fritzing 0.9.6b)
breadboards: 1

parts:
  Componente4 = Arduino Uno (Rev3)
  DS3 = DS18B20 adaptado
  DS4 = DS18B20 adaptado
  DS5 = DS18B20 adaptado
  R2 = Resistor [tolerance=±5% resistance=4.7k package="2010 [SMD]"]

nets:
  N1: Componente4.D2, DS3.DQ, DS4.DQ, DS5.DQ, R2.Pin_1
  VDD: Componente4.5V, DS3.VDD, DS4.VDD, DS5.VDD, R2.Pin_0
  GND: Componente4.GND, DS3.GND, DS4.GND, DS5.GND
