# Fritzing sketch R01_N1 (saved by Fritzing 0.9.6b)
breadboards: 1

parts:
  Componente4 = Arduino Uno (Rev3)
  part = Resistor [tolerance=±5% resistance=4.7k power=0.25 package=THT]
  DS3 = DS18B20 adaptado

nets:
  N1: Componente4.D2, part.Pin_0, DS3.DQ
  5V: Componente4.5V, part.Pin_1, DS3.VDD
  GND: Componente4.GND, DS3.GND
