# Fritzing sketch R01_N2 (saved by Fritzing 0.9.6b)
breadboards: 1

parts:
  Componente4 = Arduino Uno (Rev3)
  part = Resistor [tolerance=±5% resistance=4.7k power=0.25 package=THT]
  DS3 = DS18B20 adaptado
  LCM1602_IIC5 = LCM1602 IIC [part_number="LCM1602 IIC" chip_label="LCM1602 IIC" package="DIP (Dual Inline) [THT]"]
  LCD5 = LCD screen

nets:
  N1: Componente4.A4/SDA, LCM1602_IIC5.SDA
  N2: Componente4.A5/SCL, LCM1602_IIC5.SCL
  N3: Componente4.D2, part.Pin_0, DS3.DQ
  5V: Componente4.5V, part.Pin_1, DS3.VDD, LCM1602_IIC5.VCC
  GND: Componente4.GND, DS3.GND, LCM1602_IIC5.GND
  VSS: LCM1602_IIC5.VSS, LCD5.VSS
  VDD: LCM1602_IIC5.VDD, LCD5.VDD
  N4: LCM1602_IIC5.V0, LCD5.V0
  N5: LCM1602_IIC5.RS, LCD5.RS
  N6: LCM1602_IIC5.RW, LCD5.R/W
  N7: LCM1602_IIC5.E, LCD5.E
  N8: LCM1602_IIC5.D0, LCD5.DB0
  N9: LCM1602_IIC5.D1, LCD5.DB1
  N10: LCM1602_IIC5.D2, LCD5.DB2
  N11: LCM1602_IIC5.D3, LCD5.DB3
  N12: LCM1602_IIC5.D4, LCD5.DB4
  N13: LCM1602_IIC5.D5, LCD5.DB5
  N14: LCM1602_IIC5.D6, LCD5.DB6
  N15: LCM1602_IIC5.D7, LCD5.DB7
  N16: LCM1602_IIC5.A, LCD5.LED+
  N17: LCM1602_IIC5.K, LCD5.LED-
  N18: LCM1602_IIC5.LED_A, LCM1602_IIC5.LED_B

custom parts:
  LCM1602 IIC: I2C-Module to use a 1602 or 2004 LCD on with the wire.h libory Serial LCD Modul
