# Fritzing sketch R01_N3 (saved by Fritzing 0.9.6b)
breadboards: 1

parts:
  Componente4 = Arduino Uno (Rev3)
  part = Resistor [tolerance=±5% resistance=4.7k power=0.25 package=THT]
  DS3 = DS18B20 adaptado
  LCM1602_IIC5 = LCM1602 IIC [part_number="LCM1602 IIC" chip_label="LCM1602 IIC" package="DIP (Dual Inline) [THT]"]
  LCD5 = LCD screen
  SD_card_module5 = SD Card Module

nets:
  N1: Componente4.A4/SDA, LCM1602_IIC5.SDA
  N2: Componente4.A5/SCL, LCM1602_IIC5.SCL
  5V: Componente4.D10_PWM/SS, Componente4.5V, part.Pin_1, DS3.VDD, LCM1602_IIC5.VCC, SD_card_module5.+5, SD_card_module5.CS
  N3: Componente4.D11_PWM/MOSI, SD_card_module5.MOSI
  N4: Componente4.D12/MISO, SD_card_module5.MISO
  N5: Componente4.D13/SCK, SD_card_module5.SCK
  N6: Componente4.D2, part.Pin_0, DS3.DQ
  GND: Componente4.GND, DS3.GND, LCM1602_IIC5.GND, SD_card_module5.GND
  VSS: LCM1602_IIC5.VSS, LCD5.VSS
  VDD: LCM1602_IIC5.VDD, LCD5.VDD
  N7: LCM1602_IIC5.V0, LCD5.V0
  N8: LCM1602_IIC5.RS, LCD5.RS
  N9: LCM1602_IIC5.RW, LCD5.R/W
  N10: LCM1602_IIC5.E, LCD5.E
  N11: LCM1602_IIC5.D0, LCD5.DB0
  N12: LCM1602_IIC5.D1, LCD5.DB1
  N13: LCM1602_IIC5.D2, LCD5.DB2
  N14: LCM1602_IIC5.D3, LCD5.DB3
  N15: LCM1602_IIC5.D4, LCD5.DB4
  N16: LCM1602_IIC5.D5, LCD5.DB5
  N17: LCM1602_IIC5.D6, LCD5.DB6
  N18: LCM1602_IIC5.D7, LCD5.DB7
  N19: LCM1602_IIC5.A, LCD5.LED+
  N20: LCM1602_IIC5.K, LCD5.LED-
  N21: LCM1602_IIC5.LED_A, LCM1602_IIC5.LED_B

custom parts:
  LCM1602 IIC: I2C-Module to use a 1602 or 2004 LCD on with the wire.h libory Serial LCD Modul
  SD Card Module: SD Card Module Slot Socket Reader For Arduino ARM MCU
